# Fritzing sketch arduinosetup (saved by Fritzing 0.9.0b)
breadboards: 1

parts:
  Onderdeel1 = Arduino Uno (Rev3)
  J1 = Infrared Proximity Sensor
  J2 = Infrared Proximity Sensor

nets:
  N1: Onderdeel1.A0, J2.Vout
  N2: Onderdeel1.A1, J1.Vout
  VCC: Onderdeel1.5V, J1.Vcc, J2.Vcc
  GND: Onderdeel1.GND, J1.GND, J2.GND
