# Fritzing sketch myFirstgameFritz (saved by Fritzing 0.9.0b)
breadboards: 1

parts:
  Onderdeel1 = Arduino Uno (Rev3)
  LED1 = LED - 5mm [color="Green (555nm)" package="5 mm [THT]"]
  LED2 = LED - 5mm [color="Red (633nm)" package="5 mm [THT]"]
  R2 = Resistor [tolerance=±5% resistance=220 package=THT]
  R1 = Resistor [tolerance=±5% resistance=220 package=THT]

nets (from the schematic view):
  N1: Onderdeel1.D9_PWM, LED1.cathode
  N2: Onderdeel1.D7, LED2.cathode
  N3: Onderdeel1.GND, R2.Pin_0
  N4: LED1.anode, R2.Pin_1, R1.Pin_1
  N5: LED2.anode, R1.Pin_0
